# Fritzing sketch smashdash3001 (saved by Fritzing 0.9.4)
breadboards: 2

parts:
  Part1 = Arduino Mega 2560 (Rev3)
  U3 = RJ45 Jack [package=rj45-8]
  U4 = RJ45 Jack [package=rj45-8]
  Power_plug1 = Power plug
  S1 = Square Pushbutton
  DFRobot_DFPlayer_Mini1 = DFRobot DFPlayer Mini [part_number=DFR0299]
  C1 = Electrolytic Capacitor [capacitance=1000µF voltage=16V package="300 mil [THT, electrolytic]"]
  KY-1 = Keyes Relay [package=THT]
  R1 = Resistor [tolerance=±5% resistance=470 package="2010 [SMD]"]
  R2 = Resistor [tolerance=±5% resistance=10k package="0603 [SMD]"]
  R3 = Resistor [tolerance=±5% resistance=10k package="2010 [SMD]"]
  R4 = Resistor [tolerance=±5% resistance=470 package="2010 [SMD]"]
  R5 = Resistor [tolerance=±5% resistance=10k package="2010 [SMD]"]
  R6 = Resistor [tolerance=±5% resistance=470 package="2010 [SMD]"]
  C2 = Electrolytic Capacitor [capacitance=470µF voltage=16V package="300 mil [THT, electrolytic]"]
  U5 = RJ45 Jack [package=rj45-8]
  J1 = Piezo Speaker
  LED1 = smd LED [color="Red (633nm)" package="1206 [SMD]"]
  R7 = Resistor [tolerance=±5% resistance=1k package="2010 [SMD]"]
  R8 = Resistor [tolerance=±5% resistance=470 package="2010 [SMD]"]
  R9 = Resistor [tolerance=±5% resistance=470 package="2010 [SMD]"]

nets:
  N1: Part1.D12_PWM, R9.Pin_1
  N2: Part1.D11_PWM, R7.Pin_0
  N3: Part1.D10_PWM, DFRobot_DFPlayer_Mini1.TX
  N4: Part1.5V, U3.2, U4.2, S1.leg1, KY-1.power
  GND: Part1.GND, U3.3, U4.3, Power_plug1.GND, DFRobot_DFPlayer_Mini1.GND-1, DFRobot_DFPlayer_Mini1.GND-2, C1.-, KY-1.ground, R2.Pin_1, R3.Pin_1, R5.Pin_1, C2.-, U5.8, J1.pin1, LED1.anode, R8.Pin_1
  N5: Part1.D24, U3.1, R3.Pin_0
  N6: Part1.D25, R4.Pin_1
  N7: Part1.D28, U4.1, R2.Pin_0
  N8: Part1.D29, R1.Pin_1
  N9: Part1.D32, S1.leg0, R5.Pin_0
  N10: Part1.D33, R6.Pin_1
  N11: Part1.D36, KY-1.signal
  N12: U3.4, R4.Pin_0
  N13: U4.4, R1.Pin_0
  N14: Power_plug1.VCC, KY-1.C
  N15: DFRobot_DFPlayer_Mini1.VCC, C1.+, KY-1.NO, C2.+, U5.2
  N16: DFRobot_DFPlayer_Mini1.RX, R7.Pin_1
  N17: DFRobot_DFPlayer_Mini1.SPK_1, J1.pin2
  N18: R6.Pin_0, LED1.cathode
  N19: U5.4, R9.Pin_0
  N20: U5.6, R8.Pin_0

custom parts:
  Keyes Relay: The Keyes 5V relay module is suitable for SCM development, home appliance control. It uses a 5V~12V TIL control signal which can control DC / AC signal.
